# Fritzing sketch project IOT FINAL Sketch 4 (saved by Fritzing 0.9.3b)
breadboards: 1

parts:
  LCD1 = LCD screen
  Mod1 = KY-019 5V Relay Module [package="Breakout board"]
  F1 = Fan - Ventilador [package=THT]
  Part2 = Arduino Uno (Rev3) - ICSP
  R1 = Rotary Potentiometer (Small) [maximum_resistance=100kΩ package=THT]
  J1 = Power Jack [package=power_jack_pth]
  DHT11_1 = DHT11 module

nets:
  GND: LCD1.VSS, LCD1.R/W, LCD1.LED-, Part2.GND, R1.leg1, DHT11_1.GND
  VDD: LCD1.VDD, LCD1.LED+, Mod1.+, Mod1.-, Part2.5V, R1.leg2, DHT11_1.DATA
  N1: LCD1.V0, R1.wiper
  N2: LCD1.RS, Part2.D12/MISO
  N3: LCD1.E, Part2.ICSP_MOSI, Part2.D11_PWM/MOSI
  N4: LCD1.DB4, Part2.D6_PWM
  N5: LCD1.DB5, Part2.D5_PWM
  N6: LCD1.DB6, Part2.D4
  N7: LCD1.DB7, Part2.D3_PWM
  N8: Mod1.S, Part2.D2
  N9: Mod1.Common, J1.GND
  N10: Mod1.NO, F1.GND
  N11: F1.5V, J1.GNDBREAK
  N12: Part2.D8, DHT11_1.VCC

custom parts:
  KY-019 5V Relay Module: KY-019 5V Relay module, used to control AC circuits. (Special thanks to vanepp for fixing the PCB holes and other errors)
  Fan - Ventilador: Ventilador de 2 pines, se encuentra comunmente en computadoras de escritorio
  DHT11 module: https://cdn-learn.adafruit.com/downloads/pdf/dht.pdf DHT11 black pcb module reference by:https://github.com/adafruit/Fritzing-Library/blob/master/parts/DHT11%20Humitidy%20and%20Temperature%20Sensor.fzpz

// code stored in the sketch: Untitled3.ino
#include"DHT.h"
#include<LiquidCrystal.h>
LiquidCrystal lcd(12, 11, 6, 5, 4, 3);
DHT dht(8 , DHT11);
int temp ;
int humi ;
void setup() {

  lcd.begin(16, 2);
  dht.begin();
  
  lcd.setCursor(3, 0);
  lcd.print("DHT Sensor");
  lcd.setCursor(5, 1);
  lcd.print("Reading...");
  delay(3000);
  lcd.clear();

}

void loop() {

  delay(2000);
  temp = dht.readTemperature();
  humi = dht.readHumidity();
  lcd.setCursor(0, 0);
  lcd.print("Temperature=");
  lcd.print(temp);
  lcd.print(" C");
  
  lcd.setCursor(0, 1);
  lcd.print("Humidity =  ");
  lcd.print(humi);
  lcd.print(" %");


}
